// Logisim project cpu.circ as structural Verilog
module full_adder (
  input  IN_A,
  input  IN_B,
  input  IN_Carry,
  output Out_Carry,
  output Sum
);

  wire and_1_out, and_2_out, and_3_out;

  and and_1 (and_1_out, IN_A, IN_B);
  and and_2 (and_2_out, IN_A, IN_Carry);
  and and_3 (and_3_out, IN_B, IN_Carry);
  xor xor_1 (Sum, IN_A, IN_B, IN_Carry);
  or or_1 (Out_Carry, and_1_out, and_2_out, and_3_out);
endmodule

module adder4 (
  input  [3:0] IN_A,
  input  [3:0] IN_B,
  input  IN_Carry,
  output Out_Carry,
  output b3,
  output b2,
  output b1,
  output b0
);

  wire full_adder_2_out_carry, full_adder_3_out_carry, full_adder_4_out_carry;

  full_adder full_adder_1 (
    .IN_A(IN_A[3]), .IN_B(IN_B[3]), .IN_Carry(full_adder_2_out_carry), .Out_Carry(Out_Carry), .Sum(b3));
  full_adder full_adder_2 (
    .IN_A(IN_A[2]), .IN_B(IN_B[2]), .IN_Carry(full_adder_3_out_carry), .Out_Carry(full_adder_2_out_carry),
    .Sum(b2));
  full_adder full_adder_3 (
    .IN_A(IN_A[1]), .IN_B(IN_B[1]), .IN_Carry(full_adder_4_out_carry), .Out_Carry(full_adder_3_out_carry),
    .Sum(b1));
  full_adder full_adder_4 (
    .IN_A(IN_A[0]), .IN_B(IN_B[0]), .IN_Carry(IN_Carry), .Out_Carry(full_adder_4_out_carry), .Sum(b0));
endmodule

module adder16 (
  input  [15:0] IN_A,
  input  [15:0] IN_B,
  input  IN_Carry,
  output [16:0] Sum
);

  wire adder4_2_out_carry, adder4_3_out_carry, adder4_4_out_carry;

  adder4 adder4_1 (
    .IN_A(IN_A[15:12]), .IN_B(IN_B[15:12]), .IN_Carry(adder4_2_out_carry), .Out_Carry(Sum[16]), .b3(Sum[15]),
    .b2(Sum[14]), .b1(Sum[13]), .b0(Sum[12]));
  adder4 adder4_2 (
    .IN_A(IN_A[11:8]), .IN_B(IN_B[11:8]), .IN_Carry(adder4_3_out_carry), .Out_Carry(adder4_2_out_carry),
    .b3(Sum[11]), .b2(Sum[10]), .b1(Sum[9]), .b0(Sum[8]));
  adder4 adder4_3 (
    .IN_A(IN_A[7:4]), .IN_B(IN_B[7:4]), .IN_Carry(adder4_4_out_carry), .Out_Carry(adder4_3_out_carry),
    .b3(Sum[7]), .b2(Sum[6]), .b1(Sum[5]), .b0(Sum[4]));
  adder4 adder4_4 (
    .IN_A(IN_A[3:0]), .IN_B(IN_B[3:0]), .IN_Carry(IN_Carry), .Out_Carry(adder4_4_out_carry), .b3(Sum[3]),
    .b2(Sum[2]), .b1(Sum[1]), .b0(Sum[0]));
endmodule

module subtractor16 (
  input  [15:0] IN_A,
  input  [15:0] IN_B,
  output [16:0] Sum
);

  wire [15:0] not_1_out;

  assign not_1_out = ~IN_B;  // NOT_Gate not_1, 16 bits wide
  adder16 adder16_1 (.IN_A(IN_A), .IN_B(not_1_out), .IN_Carry(1'b1), .Sum(Sum));
endmodule

module ALU (
);

  adder16 adder16_1 (.IN_Carry(1'b0));  // open: IN_A, IN_B, Sum
  subtractor16 subtractor16_1 ();  // open: IN_A, IN_B, Sum
  // AND_Gate and_1 is placed but not wired
  // OR_Gate or_1 is placed but not wired
endmodule

module left_bit_shifter16 (
  input  [15:0] IN_A,
  output [15:0] Result
);


  assign Result = {IN_A[14:0], 1'b0};
  // also tied to GND on the sheet: IN_A[15]
endmodule

module right_bit_shifter16 (
  input  [15:0] IN_A,
  output [15:0] Result
);


  assign Result = {1'b0, IN_A[15:1]};
  // also tied to GND on the sheet: IN_A[0]
endmodule

module decoder_3x8 (
  input  [2:0] IN_A,
  output Out_0,
  output Out_1,
  output Out_2,
  output Out_3,
  output Out_4,
  output Out_5,
  output Out_6,
  output Out_7
);

  and and_1 (Out_0, ~IN_A[2], ~IN_A[1], ~IN_A[0]);  // AND_Gate
  and and_2 (Out_1, ~IN_A[2], ~IN_A[1], IN_A[0]);  // AND_Gate
  and and_3 (Out_2, ~IN_A[2], IN_A[1], ~IN_A[0]);  // AND_Gate
  and and_4 (Out_3, ~IN_A[2], IN_A[1], IN_A[0]);  // AND_Gate
  and and_5 (Out_4, IN_A[2], ~IN_A[1], ~IN_A[0]);  // AND_Gate
  and and_6 (Out_5, IN_A[2], ~IN_A[1], IN_A[0]);  // AND_Gate
  and and_7 (Out_6, IN_A[2], IN_A[1], ~IN_A[0]);  // AND_Gate
  and and_8 (Out_7, IN_A[2], IN_A[1], IN_A[0]);
endmodule
